# Fritzing sketch wiring (saved by Fritzing 0.9.3b)

parts:
  WeMos_D1_Mini2 = WeMos D1 Mini
  S1 = Pushbutton [package="[THT]"]
  DHT1 = DHT11 Humitidy and Temperature Sensor
  R1 = Resistor [tolerance=±5% resistance=4.7k package="0805 [SMD]"]

nets:
  3V3: WeMos_D1_Mini2.3V3, DHT1.VDD, R1.Pin_0
  N1: WeMos_D1_Mini2.D3, DHT1.DATA, R1.Pin_1
  N2: WeMos_D1_Mini2.D6, WeMos_D1_Mini2.G, S1.Pin_1, S1.Pin_2, DHT1.GND

custom parts:
  DHT11 Humitidy and Temperature Sensor: DHT11 Humidity and Temperature Sensor
